// Logisim project snake.circ as structural Verilog: 4 circuits, main circuit main
module main (
);

  wire and_1_out, button_2_out, button_3_out, button_4_out, button_out, clock_1_out, comparator_1_eq,
       comparator_2_eq, d_ff_1_qn, HALT_out, JMPZ_out, not_2_out, not_3_out, not_4_out, not_5_out, or_3_out,
       SPNT_out, STORE_out;
  wire [0:0] disp_1_out_37, not_1_out;
  wire [1:0] or_1_out, register_2_q;
  wire [9:0] adder_1_out, adder_2_out, multiplexer_1_out, multiplexer_2_out, multiplexer_3_out, ram_1_data,
       register_1_q, regs_1_nreg_2, regs_1_reg1_2, regs_1_reg2_2, rom_1_data_2;
  wire [25:10] rom_1_data;
  wire [31:0] disp_1_out_5, disp_1_out_6, disp_1_out_7, disp_1_out_8, disp_1_out_9, disp_1_out_10,
       disp_1_out_11, disp_1_out_12, disp_1_out_13, disp_1_out_14, disp_1_out_15, disp_1_out_16,
       disp_1_out_17, disp_1_out_18, disp_1_out_19, disp_1_out_20, disp_1_out_21, disp_1_out_22,
       disp_1_out_23, disp_1_out_24, disp_1_out_25, disp_1_out_26, disp_1_out_27, disp_1_out_28,
       disp_1_out_29, disp_1_out_30, disp_1_out_31, disp_1_out_32, disp_1_out_33, disp_1_out_34,
       disp_1_out_35, disp_1_out_36;

  Clock clock_1 (.out(clock_1_out));
  D_Flip_Flop d_ff_1 (.Qn(d_ff_1_qn), .preset(HALT_out));  // open: clk, D, Q, en, reset
  Adder #(.width(10)) adder_1 (.a(10'h1), .b(register_1_q), .out(adder_1_out));  // open: cin, cout
  Multiplexer #(.width(10)) multiplexer_1 (
    .in0(adder_1_out), .in1(regs_1_reg1_2), .out(multiplexer_1_out), .sel(JMPZ_out));  // open: en
  Register #(.width(10), .trigger("falling")) register_1 (
    .D(multiplexer_1_out), .Q(register_1_q), .clk(and_1_out));  // open: en, clr
  and and_1 (and_1_out, clock_1_out, d_ff_1_qn);
  regs regs_1 (
    .CLK(and_1_out), .REG1(rom_1_data[21:18]), .REG2(rom_1_data[17:14]), .NREG(rom_1_data[13:10]),
    .NVAL(multiplexer_3_out), .VAL(rom_1_data_2), .REG1_2(regs_1_reg1_2), .REG2_2(regs_1_reg2_2),
    .NREG_2(regs_1_nreg_2));
  Adder #(.width(10)) adder_2 (.a(regs_1_reg1_2), .b(regs_1_reg2_2), .out(adder_2_out));  // open: cin, cout
  Comparator #(.width(10)) comparator_1 (.a(regs_1_reg1_2), .b(regs_1_reg2_2), .eq(comparator_1_eq));  // open: gt, lt
  ROM #(.addrWidth(10), .dataWidth(26)) rom_1 (.addr(register_1_q), .data({rom_1_data, rom_1_data_2}));  // open: sel
  RAM #(.addrWidth(10), .dataWidth(10), .bus("separate")) ram_1 (
    .addr(regs_1_reg1_2), .din(regs_1_nreg_2), .data(ram_1_data), .clk(STORE_out));  // open: str, sel, ld, clr
  Comparator #(.width(10)) comparator_2 (.a({10{1'b0}}), .b(regs_1_reg2_2), .eq(comparator_2_eq));  // open: gt, lt
  not not_1 (not_1_out[0], comparator_1_eq);
  Multiplexer #(.select(3), .width(10)) multiplexer_2 (
    .in0(regs_1_nreg_2), .in1(regs_1_nreg_2), .in2(adder_2_out), .in3({{9{1'b0}}, not_1_out[0]}),
    .in4(regs_1_nreg_2), .in5(ram_1_data), .in6(regs_1_nreg_2), .in7({{8{1'b0}}, register_2_q}),
    .out(multiplexer_2_out), .sel(rom_1_data[24:22]));  // open: en
  Multiplexer #(.width(10)) multiplexer_3 (
    .in0(multiplexer_2_out), .in1({{9{1'b0}}, disp_1_out_37[0]}), .out(multiplexer_3_out),
    .sel(rom_1_data[25]));  // open: en
  not not_2 (not_2_out, rom_1_data[25]);
  not not_3 (not_3_out, rom_1_data[22]);
  not not_4 (not_4_out, rom_1_data[24]);
  not not_5 (not_5_out, rom_1_data[23]);
  and JMPZ (JMPZ_out, rom_1_data[22], not_4_out, not_5_out, comparator_2_eq);
  and SPNT (SPNT_out, rom_1_data[24], not_5_out, not_3_out, not_2_out, and_1_out);
  and HALT (HALT_out, not_3_out, not_5_out, not_2_out, and_1_out, not_4_out);
  and STORE (STORE_out, rom_1_data[24], rom_1_data[23], not_2_out, not_3_out, and_1_out);
  disp disp_1 (
    .\new (regs_1_nreg_2[0]), .X(regs_1_reg1_2[4:0]), .Y(regs_1_reg2_2[4:0]), .clk(SPNT_out),
    .out_5(disp_1_out_5), .out_6(disp_1_out_6), .out_7(disp_1_out_7), .out_8(disp_1_out_8),
    .out_9(disp_1_out_9), .out_10(disp_1_out_10), .out_11(disp_1_out_11), .out_12(disp_1_out_12),
    .out_13(disp_1_out_13), .out_14(disp_1_out_14), .out_15(disp_1_out_15), .out_16(disp_1_out_16),
    .out_17(disp_1_out_17), .out_18(disp_1_out_18), .out_19(disp_1_out_19), .out_20(disp_1_out_20),
    .out_21(disp_1_out_21), .out_22(disp_1_out_22), .out_23(disp_1_out_23), .out_24(disp_1_out_24),
    .out_25(disp_1_out_25), .out_26(disp_1_out_26), .out_27(disp_1_out_27), .out_28(disp_1_out_28),
    .out_29(disp_1_out_29), .out_30(disp_1_out_30), .out_31(disp_1_out_31), .out_32(disp_1_out_32),
    .out_33(disp_1_out_33), .out_34(disp_1_out_34), .out_35(disp_1_out_35), .out_36(disp_1_out_36),
    .out_37(disp_1_out_37[0]));
  DotMatrix #(.inputtype("row"), .matrixcols(32), .matrixrows(32)) dotmatrix_1 (
    .row0(disp_1_out_5), .row1(disp_1_out_6), .row2(disp_1_out_7), .row3(disp_1_out_8), .row4(disp_1_out_9),
    .row5(disp_1_out_10), .row6(disp_1_out_11), .row7(disp_1_out_12), .row8(disp_1_out_13),
    .row9(disp_1_out_14), .row10(disp_1_out_15), .row11(disp_1_out_16), .row12(disp_1_out_17),
    .row13(disp_1_out_18), .row14(disp_1_out_19), .row15(disp_1_out_20), .row16(disp_1_out_21),
    .row17(disp_1_out_22), .row18(disp_1_out_23), .row19(disp_1_out_24), .row20(disp_1_out_25),
    .row21(disp_1_out_26), .row22(disp_1_out_27), .row23(disp_1_out_28), .row24(disp_1_out_29),
    .row25(disp_1_out_30), .row26(disp_1_out_31), .row27(disp_1_out_32), .row28(disp_1_out_33),
    .row29(disp_1_out_34), .row30(disp_1_out_35), .row31(disp_1_out_36));
  Button button (.out(button_out));
  Button button_2 (.out(button_2_out));
  Button button_3 (.out(button_3_out));
  Button button_4 (.out(button_4_out));
  or or_1 (or_1_out[0], button_3_out, button_2_out);
  or or_2 (or_1_out[1], button_2_out, button_4_out);
  Register #(.width(2)) register_2 (.D(or_1_out), .Q(register_2_q), .clk(or_3_out));  // open: en, clr
  or or_3 (or_3_out, button_out, button_2_out, button_3_out, button_4_out);

  // Notes on the sheet:
  //   contents of rom_1 (hex, n*v repeats v):
  //   843c02 841000 802400 190040f 841001 190040f 841002 190040f 841003 1900410 841004 190040f 841005
  //   1900411 1441000 1441401 1114401 1441002 1441403 1114401 1441004 1441405 1114401 882c00 883000
  //   12f0401 bfe800 12f0401 1681000 a86801 1681400 1114400 bfe800 e85000 45002d a81000 905401 905bfe
  //   985c01 1582000 1902000 15c2000 1942000 a86bfe 440021 1441000 1441401 1c01800 d85c00 45c038 d85c01
  //   45c03c d85c02 45c040 d85c03 45c044 e45c01 45c048 806400 440048 e45c00 45c048 806401 440048 e45c03
  //   45c048 806402 440048 e45c02 45c048 806403 440048 e45c01 45c076 e45c02 45c058 e45c03 45c062 44006c
  //   1114401 1841000 1841401 d2d800 d71c00 99dc00 45c080 45c017 44001a 9053ff 842402 12f0400 2115800
  //   12f0401 d85801 458082 d05bff 458082 44004f 905001 842403 12f0400 2115800 12f0401 d85801 458082
  //   d05820 458082 44004f 9457ff 842400 12f0400 2115800 12f0401 d85801 458082 d45bff 458082 44004f 945401
  //   842401 12f0400 2115800 12f0401 d85801 458082 d45820 458082 44004f bc7c01 440056
endmodule

module dispriadok (
  input  clk,
  input  [4:0] X,
  input  \new ,
  output [31:0] out_4,
  output SINGLE
);

  wire demultiplexer_1_out0, demultiplexer_1_out1, demultiplexer_1_out2, demultiplexer_1_out3,
       demultiplexer_1_out4, demultiplexer_1_out5, demultiplexer_1_out6, demultiplexer_1_out7,
       demultiplexer_1_out8, demultiplexer_1_out9, demultiplexer_1_out10, demultiplexer_1_out11,
       demultiplexer_1_out12, demultiplexer_1_out13, demultiplexer_1_out14, demultiplexer_1_out15,
       demultiplexer_1_out16, demultiplexer_1_out17, demultiplexer_1_out18, demultiplexer_1_out19,
       demultiplexer_1_out20, demultiplexer_1_out21, demultiplexer_1_out22, demultiplexer_1_out23,
       demultiplexer_1_out24, demultiplexer_1_out25, demultiplexer_1_out26, demultiplexer_1_out27,
       demultiplexer_1_out28, demultiplexer_1_out29, demultiplexer_1_out30, demultiplexer_1_out31;

  Demultiplexer #(.select(5)) demultiplexer_1 (
    .out0(demultiplexer_1_out0), .out1(demultiplexer_1_out1), .out2(demultiplexer_1_out2),
    .out3(demultiplexer_1_out3), .out4(demultiplexer_1_out4), .out5(demultiplexer_1_out5),
    .out6(demultiplexer_1_out6), .out7(demultiplexer_1_out7), .out8(demultiplexer_1_out8),
    .out9(demultiplexer_1_out9), .out10(demultiplexer_1_out10), .out11(demultiplexer_1_out11),
    .out12(demultiplexer_1_out12), .out13(demultiplexer_1_out13), .out14(demultiplexer_1_out14),
    .out15(demultiplexer_1_out15), .out16(demultiplexer_1_out16), .out17(demultiplexer_1_out17),
    .out18(demultiplexer_1_out18), .out19(demultiplexer_1_out19), .out20(demultiplexer_1_out20),
    .out21(demultiplexer_1_out21), .out22(demultiplexer_1_out22), .out23(demultiplexer_1_out23),
    .out24(demultiplexer_1_out24), .out25(demultiplexer_1_out25), .out26(demultiplexer_1_out26),
    .out27(demultiplexer_1_out27), .out28(demultiplexer_1_out28), .out29(demultiplexer_1_out29),
    .out30(demultiplexer_1_out30), .out31(demultiplexer_1_out31), .in(clk), .sel(X));  // open: en
  D_Flip_Flop d_ff_1 (.clk(demultiplexer_1_out31), .D(\new ), .Q(out_4[0]));  // open: Qn, preset, en, reset
  D_Flip_Flop d_ff_2 (.clk(demultiplexer_1_out30), .D(\new ), .Q(out_4[1]));  // open: Qn, preset, en, reset
  D_Flip_Flop d_ff_3 (.clk(demultiplexer_1_out28), .D(\new ), .Q(out_4[3]));  // open: Qn, preset, en, reset
  D_Flip_Flop d_ff_4 (.clk(demultiplexer_1_out29), .D(\new ), .Q(out_4[2]));  // open: Qn, preset, en, reset
  D_Flip_Flop d_ff_5 (.clk(demultiplexer_1_out27), .D(\new ), .Q(out_4[4]));  // open: Qn, preset, en, reset
  D_Flip_Flop d_ff_6 (.clk(demultiplexer_1_out26), .D(\new ), .Q(out_4[5]));  // open: Qn, preset, en, reset
  D_Flip_Flop d_ff_7 (.clk(demultiplexer_1_out25), .D(\new ), .Q(out_4[6]));  // open: Qn, preset, en, reset
  D_Flip_Flop d_ff_8 (.clk(demultiplexer_1_out24), .D(\new ), .Q(out_4[7]));  // open: Qn, preset, en, reset
  D_Flip_Flop d_ff_9 (.clk(demultiplexer_1_out23), .D(\new ), .Q(out_4[8]));  // open: Qn, preset, en, reset
  D_Flip_Flop d_ff_10 (.clk(demultiplexer_1_out22), .D(\new ), .Q(out_4[9]));  // open: Qn, preset, en, reset
  D_Flip_Flop d_ff_11 (.clk(demultiplexer_1_out21), .D(\new ), .Q(out_4[10]));  // open: Qn, preset, en, reset
  D_Flip_Flop d_ff_12 (.clk(demultiplexer_1_out20), .D(\new ), .Q(out_4[11]));  // open: Qn, preset, en, reset
  D_Flip_Flop d_ff_13 (.clk(demultiplexer_1_out19), .D(\new ), .Q(out_4[12]));  // open: Qn, preset, en, reset
  D_Flip_Flop d_ff_14 (.clk(demultiplexer_1_out18), .D(\new ), .Q(out_4[13]));  // open: Qn, preset, en, reset
  D_Flip_Flop d_ff_15 (.clk(demultiplexer_1_out17), .D(\new ), .Q(out_4[14]));  // open: Qn, preset, en, reset
  Multiplexer #(.select(5)) multiplexer_1 (
    .in0(out_4[31]), .in1(out_4[30]), .in2(out_4[29]), .in3(out_4[28]), .in4(out_4[27]), .in5(out_4[26]),
    .in6(out_4[25]), .in7(out_4[24]), .in8(out_4[23]), .in9(out_4[22]), .in10(out_4[21]), .in11(out_4[20]),
    .in12(out_4[19]), .in13(out_4[18]), .in14(out_4[17]), .in15(out_4[16]), .in16(out_4[15]),
    .in17(out_4[14]), .in18(out_4[13]), .in19(out_4[12]), .in20(out_4[11]), .in21(out_4[10]),
    .in22(out_4[9]), .in23(out_4[8]), .in24(out_4[7]), .in25(out_4[6]), .in26(out_4[5]), .in27(out_4[4]),
    .in28(out_4[3]), .in29(out_4[2]), .in30(out_4[1]), .in31(out_4[0]), .out(SINGLE), .sel(X));  // open: en
  D_Flip_Flop d_ff_16 (.clk(demultiplexer_1_out16), .D(\new ), .Q(out_4[15]));  // open: Qn, preset, en, reset
  D_Flip_Flop d_ff_17 (.clk(demultiplexer_1_out15), .D(\new ), .Q(out_4[16]));  // open: Qn, preset, en, reset
  D_Flip_Flop d_ff_18 (.clk(demultiplexer_1_out14), .D(\new ), .Q(out_4[17]));  // open: Qn, preset, en, reset
  D_Flip_Flop d_ff_19 (.clk(demultiplexer_1_out13), .D(\new ), .Q(out_4[18]));  // open: Qn, preset, en, reset
  D_Flip_Flop d_ff_20 (.clk(demultiplexer_1_out12), .D(\new ), .Q(out_4[19]));  // open: Qn, preset, en, reset
  D_Flip_Flop d_ff_21 (.clk(demultiplexer_1_out11), .D(\new ), .Q(out_4[20]));  // open: Qn, preset, en, reset
  D_Flip_Flop d_ff_22 (.clk(demultiplexer_1_out10), .D(\new ), .Q(out_4[21]));  // open: Qn, preset, en, reset
  D_Flip_Flop d_ff_23 (.clk(demultiplexer_1_out9), .D(\new ), .Q(out_4[22]));  // open: Qn, preset, en, reset
  D_Flip_Flop d_ff_24 (.clk(demultiplexer_1_out8), .D(\new ), .Q(out_4[23]));  // open: Qn, preset, en, reset
  D_Flip_Flop d_ff_25 (.clk(demultiplexer_1_out7), .D(\new ), .Q(out_4[24]));  // open: Qn, preset, en, reset
  D_Flip_Flop d_ff_26 (.clk(demultiplexer_1_out6), .D(\new ), .Q(out_4[25]));  // open: Qn, preset, en, reset
  D_Flip_Flop d_ff_27 (.clk(demultiplexer_1_out5), .D(\new ), .Q(out_4[26]));  // open: Qn, preset, en, reset
  D_Flip_Flop d_ff_28 (.clk(demultiplexer_1_out4), .D(\new ), .Q(out_4[27]));  // open: Qn, preset, en, reset
  D_Flip_Flop d_ff_29 (.clk(demultiplexer_1_out3), .D(\new ), .Q(out_4[28]));  // open: Qn, preset, en, reset
  D_Flip_Flop d_ff_30 (.clk(demultiplexer_1_out2), .D(\new ), .Q(out_4[29]));  // open: Qn, preset, en, reset
  D_Flip_Flop d_ff_31 (.clk(demultiplexer_1_out1), .D(\new ), .Q(out_4[30]));  // open: Qn, preset, en, reset
  D_Flip_Flop d_ff_32 (.clk(demultiplexer_1_out0), .D(\new ), .Q(out_4[31]));  // open: Qn, preset, en, reset
endmodule

module disp (
  input  \new ,
  input  [4:0] X,
  input  [4:0] Y,
  input  clk,
  output [31:0] out_5,
  output [31:0] out_6,
  output [31:0] out_7,
  output [31:0] out_8,
  output [31:0] out_9,
  output [31:0] out_10,
  output [31:0] out_11,
  output [31:0] out_12,
  output [31:0] out_13,
  output [31:0] out_14,
  output [31:0] out_15,
  output [31:0] out_16,
  output [31:0] out_17,
  output [31:0] out_18,
  output [31:0] out_19,
  output [31:0] out_20,
  output [31:0] out_21,
  output [31:0] out_22,
  output [31:0] out_23,
  output [31:0] out_24,
  output [31:0] out_25,
  output [31:0] out_26,
  output [31:0] out_27,
  output [31:0] out_28,
  output [31:0] out_29,
  output [31:0] out_30,
  output [31:0] out_31,
  output [31:0] out_32,
  output [31:0] out_33,
  output [31:0] out_34,
  output [31:0] out_35,
  output [31:0] out_36,
  output out_37
);

  wire demultiplexer_1_out0, demultiplexer_1_out1, demultiplexer_1_out2, demultiplexer_1_out3,
       demultiplexer_1_out4, demultiplexer_1_out5, demultiplexer_1_out6, demultiplexer_1_out7,
       demultiplexer_1_out8, demultiplexer_1_out9, demultiplexer_1_out10, demultiplexer_1_out11,
       demultiplexer_1_out12, demultiplexer_1_out13, demultiplexer_1_out14, demultiplexer_1_out15,
       demultiplexer_1_out16, demultiplexer_1_out17, demultiplexer_1_out18, demultiplexer_1_out19,
       demultiplexer_1_out20, demultiplexer_1_out21, demultiplexer_1_out22, demultiplexer_1_out23,
       demultiplexer_1_out24, demultiplexer_1_out25, demultiplexer_1_out26, demultiplexer_1_out27,
       demultiplexer_1_out28, demultiplexer_1_out29, demultiplexer_1_out30, demultiplexer_1_out31,
       dispriadok_1_single, dispriadok_2_single, dispriadok_3_single, dispriadok_4_single,
       dispriadok_5_single, dispriadok_6_single, dispriadok_7_single, dispriadok_8_single,
       dispriadok_9_single, dispriadok_10_single, dispriadok_11_single, dispriadok_12_single,
       dispriadok_13_single, dispriadok_14_single, dispriadok_15_single, dispriadok_16_single,
       dispriadok_17_single, dispriadok_18_single, dispriadok_19_single, dispriadok_20_single,
       dispriadok_21_single, dispriadok_22_single, dispriadok_23_single, dispriadok_24_single,
       dispriadok_25_single, dispriadok_26_single, dispriadok_27_single, dispriadok_28_single,
       dispriadok_29_single, dispriadok_30_single, dispriadok_31_single, dispriadok_32_single;

  Demultiplexer #(.select(5)) demultiplexer_1 (
    .out0(demultiplexer_1_out0), .out1(demultiplexer_1_out1), .out2(demultiplexer_1_out2),
    .out3(demultiplexer_1_out3), .out4(demultiplexer_1_out4), .out5(demultiplexer_1_out5),
    .out6(demultiplexer_1_out6), .out7(demultiplexer_1_out7), .out8(demultiplexer_1_out8),
    .out9(demultiplexer_1_out9), .out10(demultiplexer_1_out10), .out11(demultiplexer_1_out11),
    .out12(demultiplexer_1_out12), .out13(demultiplexer_1_out13), .out14(demultiplexer_1_out14),
    .out15(demultiplexer_1_out15), .out16(demultiplexer_1_out16), .out17(demultiplexer_1_out17),
    .out18(demultiplexer_1_out18), .out19(demultiplexer_1_out19), .out20(demultiplexer_1_out20),
    .out21(demultiplexer_1_out21), .out22(demultiplexer_1_out22), .out23(demultiplexer_1_out23),
    .out24(demultiplexer_1_out24), .out25(demultiplexer_1_out25), .out26(demultiplexer_1_out26),
    .out27(demultiplexer_1_out27), .out28(demultiplexer_1_out28), .out29(demultiplexer_1_out29),
    .out30(demultiplexer_1_out30), .out31(demultiplexer_1_out31), .in(clk), .sel(Y));  // open: en
  dispriadok dispriadok_1 (
    .clk(demultiplexer_1_out0), .X(X), .\new (\new ), .out_4(out_5), .SINGLE(dispriadok_1_single));
  dispriadok dispriadok_2 (
    .clk(demultiplexer_1_out1), .X(X), .\new (\new ), .out_4(out_6), .SINGLE(dispriadok_2_single));
  dispriadok dispriadok_3 (
    .clk(demultiplexer_1_out2), .X(X), .\new (\new ), .out_4(out_7), .SINGLE(dispriadok_3_single));
  dispriadok dispriadok_4 (
    .clk(demultiplexer_1_out3), .X(X), .\new (\new ), .out_4(out_8), .SINGLE(dispriadok_4_single));
  dispriadok dispriadok_5 (
    .clk(demultiplexer_1_out4), .X(X), .\new (\new ), .out_4(out_9), .SINGLE(dispriadok_5_single));
  dispriadok dispriadok_6 (
    .clk(demultiplexer_1_out5), .X(X), .\new (\new ), .out_4(out_10), .SINGLE(dispriadok_6_single));
  dispriadok dispriadok_7 (
    .clk(demultiplexer_1_out6), .X(X), .\new (\new ), .out_4(out_11), .SINGLE(dispriadok_7_single));
  dispriadok dispriadok_8 (
    .clk(demultiplexer_1_out7), .X(X), .\new (\new ), .out_4(out_12), .SINGLE(dispriadok_8_single));
  dispriadok dispriadok_9 (
    .clk(demultiplexer_1_out8), .X(X), .\new (\new ), .out_4(out_13), .SINGLE(dispriadok_9_single));
  dispriadok dispriadok_10 (
    .clk(demultiplexer_1_out9), .X(X), .\new (\new ), .out_4(out_14), .SINGLE(dispriadok_10_single));
  dispriadok dispriadok_11 (
    .clk(demultiplexer_1_out10), .X(X), .\new (\new ), .out_4(out_15), .SINGLE(dispriadok_11_single));
  dispriadok dispriadok_12 (
    .clk(demultiplexer_1_out11), .X(X), .\new (\new ), .out_4(out_16), .SINGLE(dispriadok_12_single));
  dispriadok dispriadok_13 (
    .clk(demultiplexer_1_out12), .X(X), .\new (\new ), .out_4(out_17), .SINGLE(dispriadok_13_single));
  dispriadok dispriadok_14 (
    .clk(demultiplexer_1_out13), .X(X), .\new (\new ), .out_4(out_18), .SINGLE(dispriadok_14_single));
  dispriadok dispriadok_15 (
    .clk(demultiplexer_1_out14), .X(X), .\new (\new ), .out_4(out_19), .SINGLE(dispriadok_15_single));
  dispriadok dispriadok_16 (
    .clk(demultiplexer_1_out15), .X(X), .\new (\new ), .out_4(out_20), .SINGLE(dispriadok_16_single));
  dispriadok dispriadok_17 (
    .clk(demultiplexer_1_out16), .X(X), .\new (\new ), .out_4(out_21), .SINGLE(dispriadok_17_single));
  dispriadok dispriadok_18 (
    .clk(demultiplexer_1_out17), .X(X), .\new (\new ), .out_4(out_22), .SINGLE(dispriadok_18_single));
  dispriadok dispriadok_19 (
    .clk(demultiplexer_1_out18), .X(X), .\new (\new ), .out_4(out_23), .SINGLE(dispriadok_19_single));
  dispriadok dispriadok_20 (
    .clk(demultiplexer_1_out19), .X(X), .\new (\new ), .out_4(out_24), .SINGLE(dispriadok_20_single));
  dispriadok dispriadok_21 (
    .clk(demultiplexer_1_out20), .X(X), .\new (\new ), .out_4(out_25), .SINGLE(dispriadok_21_single));
  dispriadok dispriadok_22 (
    .clk(demultiplexer_1_out21), .X(X), .\new (\new ), .out_4(out_26), .SINGLE(dispriadok_22_single));
  dispriadok dispriadok_23 (
    .clk(demultiplexer_1_out22), .X(X), .\new (\new ), .out_4(out_27), .SINGLE(dispriadok_23_single));
  dispriadok dispriadok_24 (
    .clk(demultiplexer_1_out23), .X(X), .\new (\new ), .out_4(out_28), .SINGLE(dispriadok_24_single));
  dispriadok dispriadok_25 (
    .clk(demultiplexer_1_out24), .X(X), .\new (\new ), .out_4(out_29), .SINGLE(dispriadok_25_single));
  dispriadok dispriadok_26 (
    .clk(demultiplexer_1_out25), .X(X), .\new (\new ), .out_4(out_30), .SINGLE(dispriadok_26_single));
  dispriadok dispriadok_27 (
    .clk(demultiplexer_1_out26), .X(X), .\new (\new ), .out_4(out_31), .SINGLE(dispriadok_27_single));
  dispriadok dispriadok_28 (
    .clk(demultiplexer_1_out27), .X(X), .\new (\new ), .out_4(out_32), .SINGLE(dispriadok_28_single));
  dispriadok dispriadok_29 (
    .clk(demultiplexer_1_out28), .X(X), .\new (\new ), .out_4(out_33), .SINGLE(dispriadok_29_single));
  dispriadok dispriadok_30 (
    .clk(demultiplexer_1_out29), .X(X), .\new (\new ), .out_4(out_34), .SINGLE(dispriadok_30_single));
  dispriadok dispriadok_31 (
    .clk(demultiplexer_1_out30), .X(X), .\new (\new ), .out_4(out_35), .SINGLE(dispriadok_31_single));
  dispriadok dispriadok_32 (
    .clk(demultiplexer_1_out31), .X(X), .\new (\new ), .out_4(out_36), .SINGLE(dispriadok_32_single));
  Multiplexer #(.select(5)) multiplexer_1 (
    .in0(dispriadok_1_single), .in1(dispriadok_2_single), .in2(dispriadok_3_single),
    .in3(dispriadok_4_single), .in4(dispriadok_5_single), .in5(dispriadok_6_single),
    .in6(dispriadok_7_single), .in7(dispriadok_8_single), .in8(dispriadok_9_single),
    .in9(dispriadok_10_single), .in10(dispriadok_11_single), .in11(dispriadok_12_single),
    .in12(dispriadok_13_single), .in13(dispriadok_14_single), .in14(dispriadok_15_single),
    .in15(dispriadok_16_single), .in16(dispriadok_17_single), .in17(dispriadok_18_single),
    .in18(dispriadok_19_single), .in19(dispriadok_20_single), .in20(dispriadok_21_single),
    .in21(dispriadok_22_single), .in22(dispriadok_23_single), .in23(dispriadok_24_single),
    .in24(dispriadok_25_single), .in25(dispriadok_26_single), .in26(dispriadok_27_single),
    .in27(dispriadok_28_single), .in28(dispriadok_29_single), .in29(dispriadok_30_single),
    .in30(dispriadok_31_single), .in31(dispriadok_32_single), .out(out_37), .sel(Y));  // open: en
endmodule

// REGISTRE
module regs (
  input  CLK,
  input  [3:0] REG1,
  input  [3:0] REG2,
  input  [3:0] NREG,
  input  [9:0] NVAL,
  input  [9:0] VAL,
  output [9:0] REG1_2,
  output [9:0] REG2_2,
  output [9:0] NREG_2
);

  wire demultiplexer_1_out4, demultiplexer_1_out5, demultiplexer_1_out6, demultiplexer_1_out7,
       demultiplexer_1_out8, demultiplexer_1_out9, demultiplexer_1_out10, demultiplexer_1_out11,
       demultiplexer_1_out12, demultiplexer_1_out13, demultiplexer_1_out14, demultiplexer_1_out15;
  wire [4:0] random_1_out;
  wire [9:0] counter_1_q, register_1_q, register_2_q, register_3_q, register_4_q, register_5_q, register_6_q,
       register_7_q, register_8_q, register_9_q, register_10_q, register_11_q, register_12_q;
  wire [31:10] counter_1_q_2;

  Demultiplexer #(.select(4)) demultiplexer_1 (
    .out4(demultiplexer_1_out4), .out5(demultiplexer_1_out5), .out6(demultiplexer_1_out6),
    .out7(demultiplexer_1_out7), .out8(demultiplexer_1_out8), .out9(demultiplexer_1_out9),
    .out10(demultiplexer_1_out10), .out11(demultiplexer_1_out11), .out12(demultiplexer_1_out12),
    .out13(demultiplexer_1_out13), .out14(demultiplexer_1_out14), .out15(demultiplexer_1_out15), .in(CLK),
    .sel(NREG));  // open: out0, out1, out2, out3, en
  Random #(.width(5)) random_1 (.clk(CLK), .out(random_1_out));  // open: next, clr
  Counter #(.width(32), .max('hffffffff)) counter_1 (
    .Q({counter_1_q_2, counter_1_q}), .clk(CLK));  // open: load, D, count, carry, clr
  Register #(.width(10)) register_1 (.D(NVAL), .Q(register_1_q), .clk(demultiplexer_1_out4));  // open: en, clr
  Register #(.width(10)) register_2 (.D(NVAL), .Q(register_2_q), .clk(demultiplexer_1_out5));  // open: en, clr
  Register #(.width(10)) register_3 (.D(NVAL), .Q(register_3_q), .clk(demultiplexer_1_out6));  // open: en, clr
  Register #(.width(10)) register_4 (.D(NVAL), .Q(register_4_q), .clk(demultiplexer_1_out7));  // open: en, clr
  Register #(.width(10)) register_5 (.D(NVAL), .Q(register_5_q), .clk(demultiplexer_1_out8));  // open: en, clr
  Register #(.width(10)) register_6 (.D(NVAL), .Q(register_6_q), .clk(demultiplexer_1_out9));  // open: en, clr
  Register #(.width(10)) register_7 (.D(NVAL), .Q(register_7_q), .clk(demultiplexer_1_out10));  // open: en, clr
  Register #(.width(10)) register_8 (.D(NVAL), .Q(register_8_q), .clk(demultiplexer_1_out11));  // open: en, clr
  Register #(.width(10)) register_9 (.D(NVAL), .Q(register_9_q), .clk(demultiplexer_1_out12));  // open: en, clr
  Register #(.width(10)) register_10 (.D(NVAL), .Q(register_10_q), .clk(demultiplexer_1_out13));  // open: en, clr
  Register #(.width(10)) register_11 (.D(NVAL), .Q(register_11_q), .clk(demultiplexer_1_out14));  // open: en, clr
  Register #(.width(10)) register_12 (.D(NVAL), .Q(register_12_q), .clk(demultiplexer_1_out15));  // open: en, clr
  Multiplexer #(.select(4), .width(10)) multiplexer_1 (
    .in0({10{1'b0}}), .in1(VAL), .in2({{5{1'b0}}, random_1_out}), .in3(counter_1_q), .in4(register_1_q),
    .in5(register_2_q), .in6(register_3_q), .in7(register_4_q), .in8(register_5_q), .in9(register_6_q),
    .in10(register_7_q), .in11(register_8_q), .in12(register_9_q), .in13(register_10_q),
    .in14(register_11_q), .in15(register_12_q), .out(REG1_2), .sel(REG1));  // open: en
  Multiplexer #(.select(4), .width(10)) multiplexer_2 (
    .in0({10{1'b0}}), .in1(VAL), .in2({{5{1'b0}}, random_1_out}), .in3(counter_1_q), .in4(register_1_q),
    .in5(register_2_q), .in6(register_3_q), .in7(register_4_q), .in8(register_5_q), .in9(register_6_q),
    .in10(register_7_q), .in11(register_8_q), .in12(register_9_q), .in13(register_10_q),
    .in14(register_11_q), .in15(register_12_q), .out(REG2_2), .sel(REG2));  // open: en
  Multiplexer #(.select(4), .width(10)) multiplexer_3 (
    .in0({10{1'b0}}), .in1(VAL), .in2({{5{1'b0}}, random_1_out}), .in3(counter_1_q), .in4(register_1_q),
    .in5(register_2_q), .in6(register_3_q), .in7(register_4_q), .in8(register_5_q), .in9(register_6_q),
    .in10(register_7_q), .in11(register_8_q), .in12(register_9_q), .in13(register_10_q),
    .in14(register_11_q), .in15(register_12_q), .out(NREG_2), .sel(NREG));  // open: en
endmodule
